# Fritzing sketch schematic (saved by Fritzing 1.0.1rc)

parts:
  LCD1 = LCD screen
  Part1 = RFID-RC522-v2
  U1 = POT [knob_status=50% package=pot_alpha_rv16af-20]
  CPU1 = NodeMCU WROOM ESP 32
  J1 = Piezo Speaker

nets:
  N1: LCD1.V0, U1.S
  N2: LCD1.RS, CPU1.pin_11
  N3: LCD1.R/W, CPU1.pin_15
  N4: LCD1.E, CPU1.pin_10
  N5: LCD1.DB4, CPU1.pin_13
  N6: LCD1.DB5, CPU1.pin_23
  N7: LCD1.DB6, CPU1.pin_22
  N8: LCD1.DB7, CPU1.pin_12
  N9: LCD1.LED+, CPU1.pin_16
  N10: Part1.SDA, CPU1.pin_21
  N11: Part1.SCK, CPU1.pin_25
  N12: Part1.MOSI, CPU1.pin_31
  N13: Part1.MISO, Part1.IRQ, CPU1.pin_26
  N14: Part1.RST, CPU1.pin_19
  N15: Part1.3.3V, CPU1.pin_17
  N16: CPU1.pin_18, J1.pin1
  N17: CPU1.pin_24, J1.pin2

custom parts:
  RFID-RC522-v2: A simple China made RFID-RC522 Reader; do check the pin labels, as this is a MFRC522 based clone.
  NodeMCU WROOM ESP 32: 30 pol Development Kit
